# Fritzing sketch coffee-table (saved by Fritzing 0.9.9b)
breadboards: 1

parts:
  Part1 = Arduino Mega 2560 (Rev3)
  RE1 = KY-040 Rotary encoder [package="Breakout board"]
  RE2 = KY-040 Rotary encoder [package="Breakout board"]
  RE3 = KY-040 Rotary encoder [package="Breakout board"]
  LCD1 = LCD screen
  R1 = Trimmer Potentiometer [maximum_resistance=10kΩ package=THT]
  Part2 = Real Time Clock Module - DS1307 RTC Breakout Board
  Q1 = MOSFET-NCHANNEL [package=to220v]
  Q2 = MOSFET-NCHANNEL [package=to220v]
  Q3 = MOSFET-NCHANNEL [package=to220v]
  R2 = Resistor [tolerance=±5% power=0.25 resistance=220 package=THT]
  R3 = Resistor [tolerance=±5% power=0.25 resistance=220 package=THT]
  R4 = Resistor [tolerance=±5% power=0.25 resistance=220 package=THT]
  LED1 = RGB LED (com. cathode, rgb) [package="5 mm [THT]"]

nets:
  N1: Part1.D21/SCL, Part2.SCL
  N2: Part1.D20/SDA, Part2.SDA
  GND: Part1.GND, RE1.GND, RE2.GND, RE3.GND, LCD1.VSS, LCD1.R/W, LCD1.LED-, R1.leg1, Part2.GND, Q1.S, Q2.S, Q3.S
  VCC: Part1.VIN, RE1.Vcc, RE2.Vcc, RE3.Vcc, LCD1.VDD, LCD1.LED+, R1.leg2, Part2.5V, R2.Pin_0, R3.Pin_0, R4.Pin_0
  N3: Part1.D2_PWM, Q1.G, R2.Pin_1
  N4: Part1.D4_PWM, Q2.G, R4.Pin_1
  N5: Part1.D6_PWM, Q3.G, R3.Pin_1
  N6: Part1.D22, LCD1.DB7
  N7: Part1.D25, LCD1.DB6
  N8: Part1.D26, LCD1.DB5
  N9: Part1.D29, LCD1.DB4
  N10: Part1.D30, LCD1.E
  N11: Part1.D33, LCD1.RS
  N12: Part1.D42, RE1.DT
  N13: Part1.D45, RE1.CLK
  N14: Part1.D46, RE2.DT
  N15: Part1.D49, RE2.CLK
  N16: Part1.D50, RE3.DT
  N17: Part1.D53, RE3.CLK
  N18: LCD1.V0, R1.wiper
  N19: Q1.D, LED1.blue_anode
  N20: Q2.D, LED1.green_anode
  N21: Q3.D, LED1.red_anode

custom parts:
  KY-040 Rotary encoder: KY-040 Rotary Encoder with switch on breakout borad from AZ Delivery
